// Logisim project IC Implementation.circ as structural Verilog: 9 circuits, main circuit main
module main (
);

  wire _0_out, _1_out, _2_out, _3_out, _4_out, _5_out, _6_out, _7_out, _8_out, _9_out, button_1_out,
       clock_1_out, n7400_1__3__1y, n7400_1__6__2y, n7400_1__8__3y, n7400_1__11__4y, n7404_1__2__1y,
       n7404_1__4__2y, n7404_1__6__3y, n7404_1__8__4y, n7404_1__10__5y, n7404_1__12__6y, n7404_2__2__1y,
       n7404_2__4__2y, n7404_2__6__3y, n7404_2__8__4y, n7404_2__10__5y, n7404_2__12__6y, n7404_3__2__1y,
       n7404_3__4__2y, n7404_3__6__3y, n7404_3__8__4y, n7404_3__12__6y, n7425_1__6__1y, n7425_1__8__2y,
       n7432_1__3__1y, n7432_1__6__2y, n7432_1__8__3y, n7432_1__11__4y, n74148_1_a0, n74148_1_a1,
       n74148_1_a2, n74148_2_a0, n74148_2_a1, n74148_2_a2, n74148_2_eo, n74148_2_gs, n74161_1__11__o3,
       n74161_1__12__q2, n74161_1__13__q1, n74161_1__14__q0, n74198_1__4__q0, n74198_1__6__q1,
       n74198_1__8__q2, n74198_1__10__q3, n74371_1_out_13, n74371_1_out_14, n74371_1_out_15, n74371_1_out_16,
       n74371_1_out_17, n74371_1_out_18, n74371_1_out_19, n74371_1_out_20;
  wire [7:0] n74198_2__4__q0, n74198_3__4__q0, n74198_4__4__q0, n74198_5__4__q0, n74198_6__4__q0,
       n74198_7__4__q0, n74198_8__4__q0, n74198_9__4__q0;

  Button button_1 (.out(button_1_out));
  Button _0 (.out(_0_out));
  Button _1 (.out(_1_out));
  Button _2 (.out(_2_out));
  Button _3 (.out(_3_out));
  Button _4 (.out(_4_out));
  Button _5 (.out(_5_out));
  Button _6 (.out(_6_out));
  Button _7 (.out(_7_out));
  Button _8 (.out(_8_out));
  Button _9 (.out(_9_out));
  _7404 u_7404_1 (
    ._1__1A(button_1_out), ._2__1Y(n7404_1__2__1y), ._3__2A(_0_out), ._4__2Y(n7404_1__4__2y),
    ._5__3A(_1_out), ._6__3Y(n7404_1__6__3y), ._13__6A(_2_out), ._12__6Y(n7404_1__12__6y), ._11__5A(_3_out),
    ._10__5Y(n7404_1__10__5y), ._9__4A(_4_out), ._8__4Y(n7404_1__8__4y));  // open: _7__GND, _14__Vcc
  _7404 u_7404_2 (
    ._1__1A(_5_out), ._2__1Y(n7404_2__2__1y), ._3__2A(_6_out), ._4__2Y(n7404_2__4__2y), ._5__3A(_7_out),
    ._6__3Y(n7404_2__6__3y), ._13__6A(n74148_2_gs), ._12__6Y(n7404_2__12__6y), ._11__5A(_8_out),
    ._10__5Y(n7404_2__10__5y), ._9__4A(_9_out), ._8__4Y(n7404_2__8__4y));  // open: _7__GND, _14__Vcc
  _74148 u_74148_1 (
    ._7(n7404_1__2__1y), ._6(n7404_1__4__2y), ._5(n7404_1__6__3y), ._4(n7404_1__12__6y),
    ._3(n7404_1__10__5y), ._2(n7404_1__8__4y), ._1(n7404_2__2__1y), ._0(n7404_2__4__2y), .EI(n74148_2_eo),
    .A0(n74148_1_a0), .A1(n74148_1_a1), .A2(n74148_1_a2));  // open: EO, GS
  _74148 u_74148_2 (
    ._7(n7404_2__6__3y), ._6(n7404_2__10__5y), ._5(n7404_2__8__4y), ._4(1'b1), ._3(1'b1), ._2(1'b1),
    ._1(1'b1), ._0(1'b1), .EO(n74148_2_eo), .GS(n74148_2_gs), .EI(1'b0), .A0(n74148_2_a0), .A1(n74148_2_a1),
    .A2(n74148_2_a2));
  Clock clock_1 (.out(clock_1_out));
  _7425 u_7425_1 (
    ._1__1A(button_1_out), ._2__1B(_0_out), ._4__1C(_1_out), ._5__1D(_2_out), ._6__1Y(n7425_1__6__1y),
    ._7__GND(n7404_3__12__6y), ._14__Vcc(1'b1), ._13__2D(_6_out), ._12__2C(_5_out), ._10__2B(_3_out),
    ._9__2A(_4_out), ._8__2Y(n7425_1__8__2y));  // open: _3__NC, _11__NC
  _7400 u_7400_1 (
    ._1__1A(n74148_1_a0), ._2__1B(n74148_2_a0), ._3__1Y(n7400_1__3__1y), ._4__2A(n74148_1_a1),
    ._5__2B(n74148_2_a1), ._6__2Y(n7400_1__6__2y), ._13__4B(n74148_1_a2), ._12__4A(n74148_2_a2),
    ._11__4Y(n7400_1__11__4y), ._10__3B(n7432_1__11__4y), ._9__3A(clock_1_out), ._8__3Y(n7400_1__8__3y));  // open: _7__GND, _14__Vcc
  _74161 u_74161_1 (
    ._1__nMR(n7404_3__6__3y), ._2__CP(clock_1_out), ._3__D0(1'b0), ._4__D1(1'b0), ._5__D2(1'b0),
    ._6__D3(1'b0), ._7__CEP(1'b1), ._8__GND(1'b0), ._16__Vcc(1'b1), ._14__Q0(n74161_1__14__q0),
    ._13__Q1(n74161_1__13__q1), ._12__Q2(n74161_1__12__q2), ._11__O3(n74161_1__11__o3), ._10__CET(1'b1),
    ._9__nPE(1'b1));  // open: _15__TC
  _7404 u_7404_3 (
    ._1__1A(n7400_1__8__3y), ._2__1Y(n7404_3__2__1y), ._3__2A(n7425_1__8__2y), ._4__2Y(n7404_3__4__2y),
    ._5__3A(n7432_1__11__4y), ._6__3Y(n7404_3__6__3y), ._14__Vcc(1'b1), ._13__6A(1'b1),
    ._12__6Y(n7404_3__12__6y), ._11__5A(1'b1), ._10__5Y(n7404_3__12__6y), ._9__4A(n7425_1__6__1y),
    ._8__4Y(n7404_3__8__4y));  // open: _7__GND
  _74198 u_74198_1 (
    ._1__S0(1'b1), ._3__P0(n7400_1__3__1y), ._4__Q0(n74198_1__4__q0), ._5__P1(n7400_1__6__2y),
    ._6__Q1(n74198_1__6__q1), ._7__P2(n7400_1__11__4y), ._8__Q2(n74198_1__8__q2), ._9__P3(n7404_2__12__6y),
    ._10__Q3(n74198_1__10__q3), ._11__CP(n7404_3__2__1y), ._23__S1(1'b1), ._13__nMR(1'b1));  // open: _2__Dsr, _24__Vcc, _22__Dsl, _21__P7, _20__Q7, _19__P6, _18__Q6, _17__P5, _16__Q5, _15__P4, _14__Q4
  _7432 u_7432_1 (
    ._1__1A(n7404_3__4__2y), ._2__1B(_8_out), ._3__1Y(n7432_1__3__1y), ._4__2A(_9_out), ._5__2B(_7_out),
    ._6__2Y(n7432_1__6__2y), ._7__GND(n7404_3__12__6y), ._14__Vcc(1'b1), ._13__4B(n7432_1__8__3y),
    ._12__4A(n7404_3__8__4y), ._11__4Y(n7432_1__11__4y), ._10__3B(n7432_1__3__1y), ._9__3A(n7432_1__6__2y),
    ._8__3Y(n7432_1__8__3y));
  _74371 u_74371_1 (
    ._1__AD_A(n74198_1__4__q0), ._2__AD_B(n74198_1__6__q1), ._3__AD_C(n74198_1__8__q2),
    ._4__AD_D(n74198_1__10__q3), ._5__AD_E(n74161_1__14__q0), .out_13(n74371_1_out_13),
    .out_14(n74371_1_out_14), .out_16(n74371_1_out_16), .out_18(n74371_1_out_18), ._10__GND(1'b0),
    ._20__Vcc(1'b1), ._19__AD_H(n74161_1__11__o3), ._18__AD_G(n74161_1__12__q2),
    ._17__AD_F(n74161_1__13__q1), .out_15(n74371_1_out_15), .out_17(n74371_1_out_17),
    .out_19(n74371_1_out_19), .out_20(n74371_1_out_20));  // open: _16__nS_2, _15__nS_1
  _74198 u_74198_2 (
    ._1__S0(1'b1), ._3__P0(n74371_1_out_13), ._4__Q0(n74198_2__4__q0[0]), ._5__P1(n74371_1_out_14),
    ._6__Q1(n74198_2__4__q0[1]), ._7__P2(n74371_1_out_16), ._8__Q2(n74198_2__4__q0[2]),
    ._9__P3(n74371_1_out_18), ._10__Q3(n74198_2__4__q0[3]), ._11__CP(clock_1_out), ._24__Vcc(1'b1),
    ._23__S1(1'b1), ._21__P7(n74371_1_out_15), ._20__Q7(n74198_2__4__q0[7]), ._19__P6(n74371_1_out_17),
    ._18__Q6(n74198_2__4__q0[6]), ._17__P5(n74371_1_out_19), ._16__Q5(n74198_2__4__q0[5]),
    ._15__P4(n74371_1_out_20), ._14__Q4(n74198_2__4__q0[4]), ._13__nMR(n7404_3__6__3y));  // open: _2__Dsr, _22__Dsl
  _74198 u_74198_3 (
    ._1__S0(1'b1), ._3__P0(n74198_2__4__q0[0]), ._4__Q0(n74198_3__4__q0[0]), ._5__P1(n74198_2__4__q0[1]),
    ._6__Q1(n74198_3__4__q0[1]), ._7__P2(n74198_2__4__q0[2]), ._8__Q2(n74198_3__4__q0[2]),
    ._9__P3(n74198_2__4__q0[3]), ._10__Q3(n74198_3__4__q0[3]), ._11__CP(clock_1_out), ._24__Vcc(1'b1),
    ._23__S1(1'b1), ._21__P7(n74198_2__4__q0[7]), ._20__Q7(n74198_3__4__q0[7]), ._19__P6(n74198_2__4__q0[6]),
    ._18__Q6(n74198_3__4__q0[6]), ._17__P5(n74198_2__4__q0[5]), ._16__Q5(n74198_3__4__q0[5]),
    ._15__P4(n74198_2__4__q0[4]), ._14__Q4(n74198_3__4__q0[4]), ._13__nMR(n7404_3__6__3y));  // open: _2__Dsr, _22__Dsl
  _74198 u_74198_4 (
    ._1__S0(1'b1), ._3__P0(n74198_3__4__q0[0]), ._4__Q0(n74198_4__4__q0[0]), ._5__P1(n74198_3__4__q0[1]),
    ._6__Q1(n74198_4__4__q0[1]), ._7__P2(n74198_3__4__q0[2]), ._8__Q2(n74198_4__4__q0[2]),
    ._9__P3(n74198_3__4__q0[3]), ._10__Q3(n74198_4__4__q0[3]), ._11__CP(clock_1_out), ._24__Vcc(1'b1),
    ._23__S1(1'b1), ._21__P7(n74198_3__4__q0[7]), ._20__Q7(n74198_4__4__q0[7]), ._19__P6(n74198_3__4__q0[6]),
    ._18__Q6(n74198_4__4__q0[6]), ._17__P5(n74198_3__4__q0[5]), ._16__Q5(n74198_4__4__q0[5]),
    ._15__P4(n74198_3__4__q0[4]), ._14__Q4(n74198_4__4__q0[4]), ._13__nMR(n7404_3__6__3y));  // open: _2__Dsr, _22__Dsl
  _74198 u_74198_5 (
    ._1__S0(1'b1), ._3__P0(n74198_4__4__q0[0]), ._4__Q0(n74198_5__4__q0[0]), ._5__P1(n74198_4__4__q0[1]),
    ._6__Q1(n74198_5__4__q0[1]), ._7__P2(n74198_4__4__q0[2]), ._8__Q2(n74198_5__4__q0[2]),
    ._9__P3(n74198_4__4__q0[3]), ._10__Q3(n74198_5__4__q0[3]), ._11__CP(clock_1_out), ._24__Vcc(1'b1),
    ._23__S1(1'b1), ._21__P7(n74198_4__4__q0[7]), ._20__Q7(n74198_5__4__q0[7]), ._19__P6(n74198_4__4__q0[6]),
    ._18__Q6(n74198_5__4__q0[6]), ._17__P5(n74198_4__4__q0[5]), ._16__Q5(n74198_5__4__q0[5]),
    ._15__P4(n74198_4__4__q0[4]), ._14__Q4(n74198_5__4__q0[4]), ._13__nMR(n7404_3__6__3y));  // open: _2__Dsr, _22__Dsl
  DotMatrix #(.matrixcols(8), .matrixrows(8)) dotmatrix_1 (
    .col0(n74198_6__4__q0), .col1(n74198_7__4__q0), .col2(n74198_8__4__q0), .col3(n74198_9__4__q0),
    .col4(n74198_5__4__q0), .col5(n74198_4__4__q0), .col6(n74198_3__4__q0), .col7(n74198_2__4__q0));
  _74198 u_74198_6 (
    ._1__S0(1'b1), ._3__P0(n74198_7__4__q0[0]), ._4__Q0(n74198_6__4__q0[0]), ._5__P1(n74198_7__4__q0[1]),
    ._6__Q1(n74198_6__4__q0[1]), ._7__P2(n74198_7__4__q0[2]), ._8__Q2(n74198_6__4__q0[2]),
    ._9__P3(n74198_7__4__q0[3]), ._10__Q3(n74198_6__4__q0[3]), ._11__CP(clock_1_out), ._24__Vcc(1'b1),
    ._23__S1(1'b1), ._21__P7(n74198_7__4__q0[7]), ._20__Q7(n74198_6__4__q0[7]), ._19__P6(n74198_7__4__q0[6]),
    ._18__Q6(n74198_6__4__q0[6]), ._17__P5(n74198_7__4__q0[5]), ._16__Q5(n74198_6__4__q0[5]),
    ._15__P4(n74198_7__4__q0[4]), ._14__Q4(n74198_6__4__q0[4]), ._13__nMR(n7404_3__6__3y));  // open: _2__Dsr, _22__Dsl
  _74198 u_74198_7 (
    ._1__S0(1'b1), ._3__P0(n74198_8__4__q0[0]), ._4__Q0(n74198_7__4__q0[0]), ._5__P1(n74198_8__4__q0[1]),
    ._6__Q1(n74198_7__4__q0[1]), ._7__P2(n74198_8__4__q0[2]), ._8__Q2(n74198_7__4__q0[2]),
    ._9__P3(n74198_8__4__q0[3]), ._10__Q3(n74198_7__4__q0[3]), ._11__CP(clock_1_out), ._24__Vcc(1'b1),
    ._23__S1(1'b1), ._21__P7(n74198_8__4__q0[7]), ._20__Q7(n74198_7__4__q0[7]), ._19__P6(n74198_8__4__q0[6]),
    ._18__Q6(n74198_7__4__q0[6]), ._17__P5(n74198_8__4__q0[5]), ._16__Q5(n74198_7__4__q0[5]),
    ._15__P4(n74198_8__4__q0[4]), ._14__Q4(n74198_7__4__q0[4]), ._13__nMR(n7404_3__6__3y));  // open: _2__Dsr, _22__Dsl
  _74198 u_74198_8 (
    ._1__S0(1'b1), ._3__P0(n74198_9__4__q0[0]), ._4__Q0(n74198_8__4__q0[0]), ._5__P1(n74198_9__4__q0[1]),
    ._6__Q1(n74198_8__4__q0[1]), ._7__P2(n74198_9__4__q0[2]), ._8__Q2(n74198_8__4__q0[2]),
    ._9__P3(n74198_9__4__q0[3]), ._10__Q3(n74198_8__4__q0[3]), ._11__CP(clock_1_out), ._24__Vcc(1'b1),
    ._23__S1(1'b1), ._21__P7(n74198_9__4__q0[7]), ._20__Q7(n74198_8__4__q0[7]), ._19__P6(n74198_9__4__q0[6]),
    ._18__Q6(n74198_8__4__q0[6]), ._17__P5(n74198_9__4__q0[5]), ._16__Q5(n74198_8__4__q0[5]),
    ._15__P4(n74198_9__4__q0[4]), ._14__Q4(n74198_8__4__q0[4]), ._13__nMR(n7404_3__6__3y));  // open: _2__Dsr, _22__Dsl
  _74198 u_74198_9 (
    ._1__S0(1'b1), ._3__P0(n74198_5__4__q0[0]), ._4__Q0(n74198_9__4__q0[0]), ._5__P1(n74198_5__4__q0[1]),
    ._6__Q1(n74198_9__4__q0[1]), ._7__P2(n74198_5__4__q0[2]), ._8__Q2(n74198_9__4__q0[2]),
    ._9__P3(n74198_5__4__q0[3]), ._10__Q3(n74198_9__4__q0[3]), ._11__CP(clock_1_out), ._24__Vcc(1'b1),
    ._23__S1(1'b1), ._21__P7(n74198_5__4__q0[7]), ._20__Q7(n74198_9__4__q0[7]), ._19__P6(n74198_5__4__q0[6]),
    ._18__Q6(n74198_9__4__q0[6]), ._17__P5(n74198_5__4__q0[5]), ._16__Q5(n74198_9__4__q0[5]),
    ._15__P4(n74198_5__4__q0[4]), ._14__Q4(n74198_9__4__q0[4]), ._13__nMR(n7404_3__6__3y));  // open: _2__Dsr, _22__Dsl
  // also tied to GND on the sheet: n7404_3__12__6y

  // Notes on the sheet:
  //   Blank
  //   RESET
endmodule

module _74371 (
  input  _1__AD_A,
  input  _20__Vcc,
  input  _2__AD_B,
  input  _19__AD_H,
  input  _3__AD_C,
  input  _18__AD_G,
  input  _4__AD_D,
  input  _17__AD_F,
  input  _5__AD_E,
  input  _16__nS_2,
  input  _15__nS_1,
  input  _10__GND,
  output out_13,
  output out_14,
  output out_15,
  output out_16,
  output out_17,
  output out_18,
  output out_19,
  output out_20
);

  wire or_1_out;

  or or_1 (or_1_out, _16__nS_2, _15__nS_1);
  ROM rom_1 (
    .addr({_19__AD_H, _18__AD_G, _17__AD_F, _5__AD_E, _4__AD_D, _3__AD_C, _2__AD_B, _1__AD_A}),
    .data({out_15, out_17, out_19, out_20, out_18, out_16, out_14, out_13}), .sel(or_1_out));

  // Notes on the sheet:
  //   contents of rom_1 (hex, n*v repeats v):
  //   49*0 3e 0 21 22 c 72 1e 60 36 30 6*0 45 21 43 49 14 51 29 47 49 49 6*0 49 7f 45 49 24 51 49 48 49 49
  //   6*0 51 1 49 49 7f 51 49 50 49 4a 6*0 3e 0 31 36 4 4e 6 60 36 3c 54*0 3e 0 21 22 c 72 1e 60 36 30 6*0
  //   45 21 43 49 14 51 29 47 49 49 6*0 49 7f 45 49 24 51 49 48 49 49 6*0 51 1 49 49 7f 51 49 50 49 4a 6*0
  //   3e 0 31 36 4 4e 6 60 36 3c
endmodule

module _74148 (
  input  _7,
  input  _6,
  input  _5,
  input  _4,
  input  _3,
  input  _2,
  input  _1,
  input  _0,
  input  EI,
  output EO,
  output GS,
  output A0,
  output A1,
  output A2
);

  wire and_1_out, and_2_out, and_3_out, and_4_out, and_5_out, and_6_out, and_7_out, and_8_out, and_9_out,
       and_10_out, and_11_out, and_12_out, not_1_out, not_2_out, not_3_out, not_4_out, not_5_out, not_6_out,
       not_7_out, not_8_out, not_9_out, not_10_out, not_11_out, not_12_out;

  not not_1 (not_1_out, _5);
  not not_2 (not_2_out, _4);
  not not_3 (not_3_out, _3);
  not not_4 (not_4_out, _2);
  not not_5 (not_5_out, _1);
  not not_6 (not_6_out, _0);
  not not_7 (not_7_out, _6);
  not not_8 (not_8_out, not_1_out);
  not not_9 (not_9_out, not_3_out);
  not not_10 (not_10_out, not_4_out);
  not not_11 (not_11_out, not_5_out);
  not not_12 (not_12_out, EI);
  nand nand_1 (EO, _7, _6, _5, _4, _3, _2, _1, _0, not_12_out);
  and and_1 (and_1_out, not_7_out, not_8_out, not_9_out, not_11_out, not_12_out);
  and and_2 (and_2_out, not_2_out, not_9_out, not_11_out, not_12_out);
  and and_3 (and_3_out, not_4_out, not_11_out, not_12_out);
  and and_4 (and_4_out, not_6_out, not_12_out);
  and and_5 (and_5_out, not_1_out, not_9_out, not_10_out, not_12_out);
  and and_6 (and_6_out, not_2_out, not_9_out, not_10_out, not_12_out);
  and and_7 (and_7_out, not_5_out, not_12_out);
  and and_8 (and_8_out, not_6_out, not_12_out);
  and and_9 (and_9_out, not_3_out, not_12_out);
  and and_10 (and_10_out, not_4_out, not_12_out);
  and and_11 (and_11_out, not_5_out, not_12_out);
  and and_12 (and_12_out, not_6_out, not_12_out);
  nand nand_2 (GS, EO, not_12_out);
  nor nor_1 (A0, and_1_out, and_2_out, and_3_out, and_4_out);
  nor nor_2 (A1, and_5_out, and_6_out, and_7_out, and_8_out);
  nor nor_3 (A2, and_9_out, and_10_out, and_11_out, and_12_out);

  // Notes on the sheet:
  //   Active 0
  //   Inputs
  //   Enable Out
  //   Enable In
  //   Group Select
  //   lsb
  //   Active 0
  //   Outputs
  //   msb
endmodule

module _7404 (
  input  _1__1A,
  input  _14__Vcc,
  input  _13__6A,
  input  _3__2A,
  input  _11__5A,
  input  _5__3A,
  input  _9__4A,
  input  _7__GND,
  output _2__1Y,
  output _12__6Y,
  output _4__2Y,
  output _10__5Y,
  output _6__3Y,
  output _8__4Y
);

  not not_1 (_2__1Y, _1__1A);
  not not_2 (_4__2Y, _3__2A);
  not not_3 (_6__3Y, _5__3A);
  not not_4 (_12__6Y, _13__6A);
  not not_5 (_10__5Y, _11__5A);
  not not_6 (_8__4Y, _9__4A);
endmodule

module _74161 (
  input  _1__nMR,
  input  _16__Vcc,
  input  _2__CP,
  input  _3__D0,
  input  _4__D1,
  input  _5__D2,
  input  _6__D3,
  input  _7__CEP,
  input  _10__CET,
  input  _8__GND,
  input  _9__nPE,
  output _15__TC,
  output _14__Q0,
  output _13__Q1,
  output _12__Q2,
  output _11__O3
);

  wire and_1_out, counter_1_carry, not_1_out, not_2_out;

  not not_1 (not_1_out, _1__nMR);
  and and_1 (and_1_out, _7__CEP, _9__nPE, _10__CET);
  Counter #(.width(4), .max('hf)) counter_1 (
    .load(not_2_out), .D({_6__D3, _5__D2, _4__D1, _3__D0}), .count(and_1_out),
    .Q({_11__O3, _12__Q2, _13__Q1, _14__Q0}), .carry(counter_1_carry), .clk(_2__CP), .clr(not_1_out));
  and and_2 (_15__TC, counter_1_carry, _10__CET);
  not not_2 (not_2_out, _9__nPE);
endmodule

module _74198 (
  input  _1__S0,
  input  _24__Vcc,
  input  _2__Dsr,
  input  _23__S1,
  input  _3__P0,
  input  _22__Dsl,
  input  _21__P7,
  input  _5__P1,
  input  _19__P6,
  input  _7__P2,
  input  _17__P5,
  input  _9__P3,
  input  _15__P4,
  input  _11__CP,
  input  _13__nMR,
  output _4__Q0,
  output _20__Q7,
  output _6__Q1,
  output _18__Q6,
  output _8__Q2,
  output _16__Q5,
  output _10__Q3,
  output _14__Q4
);

  wire and_1_out, and_2_out, and_3_out, and_4_out, and_5_out, and_6_out, and_7_out, and_8_out, and_9_out,
       and_10_out, and_11_out, and_12_out, and_13_out, and_14_out, and_15_out, and_16_out, and_17_out,
       and_18_out, and_19_out, and_20_out, and_21_out, and_22_out, and_23_out, and_24_out, and_25_out,
       nor_1_out, not_1_out, not_2_out, not_3_out, or_1_out, or_2_out, or_3_out, or_4_out, or_5_out,
       or_6_out, or_7_out, or_8_out, or_9_out;

  not not_1 (not_1_out, _1__S0);
  not not_2 (not_2_out, _23__S1);
  nor nor_1 (nor_1_out, not_1_out, not_2_out);
  and and_1 (and_1_out, not_2_out, not_1_out);
  and and_2 (and_2_out, _22__Dsl, not_1_out);
  and and_3 (and_3_out, _21__P7, nor_1_out);
  and and_4 (and_4_out, _18__Q6, not_2_out);
  and and_5 (and_5_out, _20__Q7, not_1_out);
  and and_6 (and_6_out, _19__P6, nor_1_out);
  and and_7 (and_7_out, _16__Q5, not_2_out);
  and and_8 (and_8_out, _18__Q6, not_1_out);
  and and_9 (and_9_out, _17__P5, nor_1_out);
  and and_10 (and_10_out, _14__Q4, not_2_out);
  and and_11 (and_11_out, _16__Q5, not_1_out);
  and and_12 (and_12_out, _15__P4, nor_1_out);
  and and_13 (and_13_out, _10__Q3, not_2_out);
  and and_14 (and_14_out, _14__Q4, not_1_out);
  and and_15 (and_15_out, _9__P3, nor_1_out);
  and and_16 (and_16_out, _8__Q2, not_2_out);
  and and_17 (and_17_out, _10__Q3, not_1_out);
  and and_18 (and_18_out, _7__P2, nor_1_out);
  and and_19 (and_19_out, _6__Q1, not_2_out);
  and and_20 (and_20_out, _8__Q2, not_1_out);
  and and_21 (and_21_out, _5__P1, nor_1_out);
  and and_22 (and_22_out, _4__Q0, not_2_out);
  and and_23 (and_23_out, _6__Q1, not_1_out);
  and and_24 (and_24_out, _3__P0, nor_1_out);
  and and_25 (and_25_out, _2__Dsr, not_2_out);
  or or_1 (or_1_out, _11__CP, and_1_out);
  or or_2 (or_2_out, and_2_out, and_3_out, and_4_out);
  or or_3 (or_3_out, and_5_out, and_6_out, and_7_out);
  or or_4 (or_4_out, and_8_out, and_9_out, and_10_out);
  or or_5 (or_5_out, and_11_out, and_12_out, and_13_out);
  or or_6 (or_6_out, and_14_out, and_15_out, and_16_out);
  or or_7 (or_7_out, and_17_out, and_18_out, and_19_out);
  or or_8 (or_8_out, and_20_out, and_21_out, and_22_out);
  or or_9 (or_9_out, and_23_out, and_24_out, and_25_out);
  D_Flip_Flop d_ff_1 (.clk(or_1_out), .D(or_2_out), .Q(_20__Q7), .reset(not_3_out));  // open: Qn, preset, en
  D_Flip_Flop d_ff_2 (.clk(or_1_out), .D(or_3_out), .Q(_18__Q6), .reset(not_3_out));  // open: Qn, preset, en
  D_Flip_Flop d_ff_3 (.clk(or_1_out), .D(or_4_out), .Q(_16__Q5), .reset(not_3_out));  // open: Qn, preset, en
  D_Flip_Flop d_ff_4 (.clk(or_1_out), .D(or_5_out), .Q(_14__Q4), .reset(not_3_out));  // open: Qn, preset, en
  not not_3 (not_3_out, _13__nMR);
  D_Flip_Flop d_ff_5 (.clk(or_1_out), .D(or_6_out), .Q(_10__Q3), .reset(not_3_out));  // open: Qn, preset, en
  D_Flip_Flop d_ff_6 (.clk(or_1_out), .D(or_7_out), .Q(_8__Q2), .reset(not_3_out));  // open: Qn, preset, en
  D_Flip_Flop d_ff_7 (.clk(or_1_out), .D(or_8_out), .Q(_6__Q1), .reset(not_3_out));  // open: Qn, preset, en
  D_Flip_Flop d_ff_8 (.clk(or_1_out), .D(or_9_out), .Q(_4__Q0), .reset(not_3_out));  // open: Qn, preset, en
endmodule

module _7400 (
  input  _1__1A,
  input  _14__Vcc,
  input  _2__1B,
  input  _13__4B,
  input  _12__4A,
  input  _4__2A,
  input  _5__2B,
  input  _10__3B,
  input  _9__3A,
  input  _7__GND,
  output _3__1Y,
  output _11__4Y,
  output _6__2Y,
  output _8__3Y
);

  nand nand_1 (_3__1Y, _2__1B, _1__1A);
  nand nand_2 (_6__2Y, _5__2B, _4__2A);
  nand nand_3 (_11__4Y, _13__4B, _12__4A);
  nand nand_4 (_8__3Y, _10__3B, _9__3A);

  // Notes on the sheet:
  //   7400: quad NAND
endmodule

module _7432 (
  input  _1__1A,
  input  _14__Vcc,
  input  _2__1B,
  input  _13__4B,
  input  _12__4A,
  input  _4__2A,
  input  _5__2B,
  input  _10__3B,
  input  _9__3A,
  input  _7__GND,
  output _3__1Y,
  output _11__4Y,
  output _6__2Y,
  output _8__3Y
);

  or or_1 (_3__1Y, _2__1B, _1__1A);
  or or_2 (_6__2Y, _5__2B, _4__2A);
  or or_3 (_11__4Y, _13__4B, _12__4A);
  or or_4 (_8__3Y, _10__3B, _9__3A);
endmodule

module _7425 (
  input  _1__1A,
  input  _14__Vcc,
  input  _2__1B,
  input  _13__2D,
  input  _3__NC,
  input  _12__2C,
  input  _4__1C,
  input  _11__NC,
  input  _5__1D,
  input  _10__2B,
  input  _9__2A,
  input  _7__GND,
  output _6__1Y,
  output _8__2Y
);

  nor nor_1 (_6__1Y, _5__1D, _4__1C, _2__1B, _1__1A);
  nor nor_2 (_8__2Y, _13__2D, _12__2C, _10__2B, _9__2A);

  // Notes on the sheet:
  //   7425: dual 4-input NOR
endmodule
