// Logisim project Incrementor-Decrementor.circ as structural Verilog: 1 circuit, main circuit main
module main (
);

  wire Add_1_out, and_1_out, button_1_out, clock_1_out, or_1_out, priority_encoder_1_p2,
       priority_encoder_1_p3, priority_encoder_1_p4, priority_encoder_1_p5, priority_encoder_1_p6,
       priority_encoder_1_p7, priority_encoder_1_p8, priority_encoder_1_p9, priority_encoder_1_p10,
       priority_encoder_1_p11, priority_encoder_1_p12, priority_encoder_1_p13, t_ff_1_q;
  wire [3:0] counter_1_q, priority_encoder_1_p1;
  wire [7:0] register_1_q, register_2_q, register_3_q, register_4_q, register_5_q, register_6_q,
       register_7_q, rom_1_data;
  wire [7:4] counter_2_q;

  Clock clock_1 (.out(clock_1_out));
  Counter #(.width(4), .max('hf)) counter_1 (
    .count(clock_1_out), .Q(counter_1_q), .clk(clock_1_out), .clr(or_1_out));  // open: load, D, carry
  and and_1 (and_1_out, counter_2_q[7], counter_2_q[5]);
  ROM rom_1 (.addr({counter_2_q, counter_1_q}), .data(rom_1_data));  // open: sel
  Counter #(.width(4), .max('hf)) counter_2 (
    .load(priority_encoder_1_p2), .D(priority_encoder_1_p1), .count(t_ff_1_q), .Q(counter_2_q),
    .clk(or_1_out), .clr(and_1_out));  // open: carry
  or or_1 (or_1_out, priority_encoder_1_p2, Add_1_out);
  DotMatrix #(.matrixcols(7), .matrixrows(8)) dotmatrix_1 (
    .col0(register_1_q), .col1(register_2_q), .col2(register_3_q), .col3(register_4_q), .col4(register_5_q),
    .col5(register_6_q), .col6(register_7_q));
  Register register_1 (.D(register_2_q), .Q(register_1_q), .clk(clock_1_out), .clr(or_1_out));  // open: en
  // Priority_Encoder #(.select(4)) priority_encoder_1: pin names not known; wires that end beside it: priority_encoder_1_p1, priority_encoder_1_p2, priority_encoder_1_p3, priority_encoder_1_p4, priority_encoder_1_p5, priority_encoder_1_p6, priority_encoder_1_p7, priority_encoder_1_p8, priority_encoder_1_p9, priority_encoder_1_p10, priority_encoder_1_p11, priority_encoder_1_p12, priority_encoder_1_p13, 1'b0, 1'b0, 1'b0, 1'b0, 1'b0
  Register register_2 (.D(register_3_q), .Q(register_2_q), .clk(clock_1_out), .clr(or_1_out));  // open: en
  Register register_3 (.D(register_4_q), .Q(register_3_q), .clk(clock_1_out), .clr(or_1_out));  // open: en
  Register register_4 (.D(register_5_q), .Q(register_4_q), .clk(clock_1_out), .clr(or_1_out));  // open: en
  Button _1 (.out(priority_encoder_1_p4));
  Button _0 (.out(priority_encoder_1_p3));
  T_Flip_Flop t_ff_1 (.clk(button_1_out), .T(button_1_out), .Q(t_ff_1_q));  // open: Qn, preset, reset, en
  Register register_5 (.D(register_6_q), .Q(register_5_q), .clk(clock_1_out), .clr(or_1_out));  // open: en
  Button _2 (.out(priority_encoder_1_p5));
  Button _3 (.out(priority_encoder_1_p6));
  Register register_6 (.D(register_7_q), .Q(register_6_q), .clk(clock_1_out), .clr(or_1_out));  // open: en
  Register register_7 (.D(rom_1_data), .Q(register_7_q), .clk(clock_1_out), .clr(or_1_out));  // open: en
  Button _4 (.out(priority_encoder_1_p7));
  Button _5 (.out(priority_encoder_1_p8));
  Button Add_1 (.out(Add_1_out));
  Button Sub_1 (.out(priority_encoder_1_p13));
  Button _7 (.out(priority_encoder_1_p10));
  Button _6 (.out(priority_encoder_1_p9));
  Button button_1 (.out(button_1_out));
  Button _9 (.out(priority_encoder_1_p12));
  Button _8 (.out(priority_encoder_1_p11));

  // Notes on the sheet:
  //   contents of rom_1 (hex, n*v repeats v):
  //   0 0 0 3e 45 49 51 3e 0 0 0 3e 45 49 51 3e 4*0 21 7f 1 5*0 21 7f 1 4*0 21 43 45 49 31 0 0 0 21 43 45
  //   49 31 0 0 0 22 49 49 49 36 0 0 0 22 49 49 49 36 0 0 0 c 14 24 7f 4 0 0 0 c 14 24 7f 4 0 0 0 72 51 51
  //   51 4e 0 0 0 72 51 51 51 4e 0 0 0 1e 29 49 49 6 0 0 0 1e 29 49 49 6 0 0 0 60 47 48 50 60 0 0 0 60 47
  //   48 50 60 0 0 0 36 49 49 49 36 0 0 0 36 49 49 49 36 0 0 0 30 49 49 4a 3c 0 0 0 30 49 49 4a 3c
  //   On/Off for Incrementer-Decrementer
endmodule
