// Logisim project Logisim Implementation.circ as structural Verilog: 1 circuit, main circuit main
module main (
  input  On_Off
);

  wire and_1_out, Clk_out, priority_encoder_1_p3, priority_encoder_1_p5, priority_encoder_1_p6,
       priority_encoder_1_p7, priority_encoder_1_p8, priority_encoder_1_p9, priority_encoder_1_p10,
       priority_encoder_1_p11, priority_encoder_1_p12, priority_encoder_1_p13, priority_encoder_1_p14,
       priority_encoder_1_p15;
  wire [3:0] Counter_q, priority_encoder_1_p2, Reg1_q;
  wire [7:0] Reg2_q, Reg3_q, Reg4_q, Reg5_q, Reg6_q, Reg7_q, rom_1_data;

  Counter #(.width(4), .max('hf)) Counter (
    .count(On_Off), .Q(Counter_q), .clk(Clk_out), .clr(priority_encoder_1_p3));  // open: load, D, carry
  Clock Clk (.out(Clk_out));
  and and_1 (and_1_out, priority_encoder_1_p3, Clk_out);
  DotMatrix #(.matrixcols(7), .matrixrows(8)) dotmatrix_1 (
    .col0(Reg7_q), .col1(Reg6_q), .col2(Reg5_q), .col3(Reg4_q), .col4(Reg3_q), .col5(Reg2_q),
    .col6(rom_1_data));
  Register Reg7 (.D(Reg6_q), .en(On_Off), .Q(Reg7_q), .clk(Clk_out), .clr(priority_encoder_1_p3));
  Register #(.width(4)) Reg1 (.D(priority_encoder_1_p2), .en(On_Off), .Q(Reg1_q), .clk(and_1_out));  // open: clr
  Register Reg6 (.D(Reg5_q), .en(On_Off), .Q(Reg6_q), .clk(Clk_out), .clr(priority_encoder_1_p3));
  // Priority_Encoder #(.select(4)) priority_encoder_1: pin names not known; wires that end beside it: On_Off, priority_encoder_1_p2, priority_encoder_1_p3, On_Off, priority_encoder_1_p5, priority_encoder_1_p6, priority_encoder_1_p7, priority_encoder_1_p8, priority_encoder_1_p9, priority_encoder_1_p10, priority_encoder_1_p11, priority_encoder_1_p12, priority_encoder_1_p13, priority_encoder_1_p14, priority_encoder_1_p15, 1'b0, 1'b0, 1'b0, 1'b0, 1'b0
  Register Reg5 (.D(Reg4_q), .en(On_Off), .Q(Reg5_q), .clk(Clk_out), .clr(priority_encoder_1_p3));
  Register Reg4 (.D(Reg3_q), .en(On_Off), .Q(Reg4_q), .clk(Clk_out), .clr(priority_encoder_1_p3));
  Button Blank (.out(priority_encoder_1_p5));
  Button _0 (.out(priority_encoder_1_p6));
  Button _1 (.out(priority_encoder_1_p7));
  Button _2 (.out(priority_encoder_1_p8));
  Button _3 (.out(priority_encoder_1_p9));
  Button _4 (.out(priority_encoder_1_p10));
  Button _5 (.out(priority_encoder_1_p11));
  Button _6 (.out(priority_encoder_1_p12));
  Button _7 (.out(priority_encoder_1_p13));
  Button _8 (.out(priority_encoder_1_p14));
  Button _9 (.out(priority_encoder_1_p15));
  Register Reg3 (.D(Reg2_q), .en(On_Off), .Q(Reg3_q), .clk(Clk_out), .clr(priority_encoder_1_p3));
  Register Reg2 (.D(rom_1_data), .en(On_Off), .Q(Reg2_q), .clk(Clk_out), .clr(priority_encoder_1_p3));
  ROM rom_1 (.addr({Reg1_q, Counter_q}), .data(rom_1_data));  // open: sel

  // Notes on the sheet:
  //   contents of rom_1 (hex, n*v repeats v):
  //   19*0 3e 45 49 51 3e 0 0 0 3e 45 49 51 3e 4*0 21 7f 1 5*0 21 7f 1 4*0 21 43 45 49 31 0 0 0 21 43 45
  //   49 31 0 0 0 22 49 49 49 36 0 0 0 22 49 49 49 36 0 0 0 c 14 24 7f 4 0 0 0 c 14 24 7f 4 0 0 0 72 51 51
  //   51 4e 0 0 0 72 51 51 51 4e 0 0 0 1e 29 49 49 6 0 0 0 1e 29 49 49 6 0 0 0 60 47 48 50 60 0 0 0 60 47
  //   48 50 60 0 0 0 36 49 49 49 36 0 0 0 36 49 49 49 36 0 0 0 30 49 49 4a 3c 0 0 0 30 49 49 4a 3c
endmodule
