// Logisim project WithoutROM.circ as structural Verilog: 1 circuit, main circuit main
module main (
  input  SWITCH
);

  wire _0_out, _1_out, _2_out, _3_out, _4_out, _5_out, _6_out, _7_out, _8_out, _9_out, C_out, clock_1_out,
       undriven;
  wire [2:0] counter_1_q;
  wire [3:0] priority_encoder_1_out, register_6_q;
  wire [4:0] multiplexer_1_out, register_1_q, register_2_q, register_3_q, register_4_q, register_5_q;
  wire [14:0] multiplexer_6_out;

  Clock clock_1 (.out(clock_1_out));
  Register #(.width(5)) register_1 (
    .D(multiplexer_1_out), .en(SWITCH), .Q(register_1_q), .clk(clock_1_out), .clr(undriven));
  Register #(.width(5)) register_2 (.D(register_1_q), .en(SWITCH), .Q(register_2_q), .clk(clock_1_out), .clr(undriven));
  Counter #(.width(3), .max('h6)) counter_1 (
    .count(SWITCH), .Q(counter_1_q), .clk(clock_1_out), .clr(undriven));  // open: load, D, carry
  Register #(.width(5)) register_3 (.D(register_2_q), .en(SWITCH), .Q(register_3_q), .clk(clock_1_out), .clr(undriven));
  Register #(.width(5)) register_4 (.D(register_5_q), .en(SWITCH), .Q(register_4_q), .clk(clock_1_out), .clr(undriven));
  Register #(.width(5)) register_5 (.D(register_3_q), .en(SWITCH), .Q(register_5_q), .clk(clock_1_out), .clr(undriven));
  Multiplexer #(.select(3), .enable("false")) multiplexer_1 (
    .in0(1'b0), .in1(1'b0), .in2(1'b0), .in3(1'b0), .in4(multiplexer_6_out[14]), .in5(multiplexer_6_out[13]),
    .in6(multiplexer_6_out[12]), .out(multiplexer_1_out[0]), .sel(counter_1_q));  // open: in7
  Multiplexer #(.select(3), .enable("false")) multiplexer_2 (
    .in0(1'b0), .in1(1'b0), .in2(1'b0), .in3(1'b0), .in4(multiplexer_6_out[11]), .in5(multiplexer_6_out[10]),
    .in6(multiplexer_6_out[9]), .out(multiplexer_1_out[1]), .sel(counter_1_q));  // open: in7
  Multiplexer #(.select(3), .enable("false")) multiplexer_3 (
    .in0(1'b0), .in1(1'b0), .in2(1'b0), .in3(1'b0), .in4(multiplexer_6_out[8]), .in5(multiplexer_6_out[7]),
    .in6(multiplexer_6_out[6]), .out(multiplexer_1_out[2]), .sel(counter_1_q));  // open: in7
  Multiplexer #(.select(3), .enable("false")) multiplexer_4 (
    .in0(1'b0), .in1(1'b0), .in2(1'b0), .in3(1'b0), .in4(multiplexer_6_out[5]), .in5(multiplexer_6_out[4]),
    .in6(multiplexer_6_out[3]), .out(multiplexer_1_out[3]), .sel(counter_1_q));  // open: in7
  Multiplexer #(.select(3), .enable("false")) multiplexer_5 (
    .in0(1'b0), .in1(1'b0), .in2(1'b0), .in3(1'b0), .in4(multiplexer_6_out[2]), .in5(multiplexer_6_out[1]),
    .in6(multiplexer_6_out[0]), .out(multiplexer_1_out[4]), .sel(counter_1_q));  // open: in7
  DotMatrix #(.matrixrows(5)) dotmatrix_1 (
    .col0(register_1_q), .col1(register_2_q), .col2(register_3_q), .col3(register_5_q), .col4(register_4_q));
  Button _0 (.out(_0_out));
  Button _3 (.out(_3_out));
  Button _1 (.out(_1_out));
  Button _2 (.out(_2_out));
  Priority_Encoder #(.select(4)) priority_encoder_1 (
    .in0(_0_out), .in1(_1_out), .in2(_2_out), .in3(_3_out), .in4(_4_out), .in5(_5_out), .in6(_6_out),
    .in7(_7_out), .in8(_8_out), .in9(_9_out), .in10(C_out), .out(priority_encoder_1_out));  // open: in11, in12, in13, in14, in15
  Button _6 (.out(_6_out));
  Button _4 (.out(_4_out));
  Button _5 (.out(_5_out));
  Multiplexer #(.select(4), .width(15), .enable("false")) multiplexer_6 (
    .in0(15'h7b6f), .in1(15'h4924), .in2(15'h73e7), .in3(15'h79e7), .in4(15'h49ed), .in5(15'h79cf),
    .in6(15'h7bcf), .in7(15'h2493), .in8(15'h7bef), .in9(15'h49ef), .in10({15{1'b0}}),
    .out(multiplexer_6_out), .sel(register_6_q));  // open: in11, in12, in13, in14, in15
  Button C (.out(C_out));
  Button _7 (.out(_7_out));
  Button _8 (.out(_8_out));
  Button _9 (.out(_9_out));
  Register #(.width(4), .trigger("high")) register_6 (
    .D(priority_encoder_1_out), .Q(register_6_q), .clk(undriven));  // open: en, clr
endmodule
